# Fritzing sketch Scout-Fritzing (saved by Fritzing 0.9.4)
circuit board: 6.24942cm x 5.44015cm
breadboards: 1

parts:
  U1 = atmega328 [package=dip]
  Y1 = CRYSTAL [package=hc49u-v]
  PAIR_SW = Pushbutton [package="[THT]"]
  RESET_SW = Pushbutton [package="[THT]"]
  C1 = Ceramic Capacitor [capacitance=22pF package="100 mil [THT, multilayer]"]
  R2 = Resistor [tolerance=±5% resistance=220 package=THT]
  R1 = Resistor [tolerance=±5% resistance=1k package=THT]
  C3 = Electrolytic Capacitor [capacitance=10µF package="100 mil [THT, electrolytic]"]
  PWR_LED = LED - 5mm [color="Red (633nm)" package="5 mm [THT]"]
  PAIR_LED = LED - 5mm [color="Green (555nm)" package="5 mm [THT]"]
  PWR_SW = Toggle Switch [package=THT]
  C2 = Ceramic Capacitor [capacitance=22pF package="100 mil [THT, multilayer]"]
  SIM7100E = SIMCOM 7100E DevKit [package=THT]
  +5V_DC = Power plug
  R3 = Resistor [tolerance=±5% resistance=220 package=THT]

nets:
  N1: U1.RESET, RESET_SW.Pin_3, RESET_SW.Pin_4, R1.Pin_1
  N2: U1.D0_(RX), SIM7100E.T
  N3: U1.D1_(TX), SIM7100E.R
  N4: U1.D2, SIM7100E.K
  N5: U1.D3_(PWM), SIM7100E.S
  5V: U1.VCC, U1.AVCC, U1.AREF, R1.Pin_0, C3.+, PWR_SW.COM, SIM7100E.V
  GND: U1.GND, PAIR_SW.Pin_3, PAIR_SW.Pin_4, RESET_SW.Pin_1, RESET_SW.Pin_2, C1.0, R2.Pin_0, C3.-, C2.1, SIM7100E.G, +5V_DC.GND, R3.Pin_0
  N6: U1.XLAT1, Y1.2, C1.1
  N7: U1.XLAT2, Y1.1, C2.0
  N8: U1.D6_(PWM), PAIR_SW.Pin_1, PAIR_SW.Pin_2
  N9: U1.D7, PWR_LED.anode
  N10: U1.D8, PAIR_LED.anode
  N11: R2.Pin_1, PWR_LED.cathode
  N12: PAIR_LED.cathode, R3.Pin_1
  N13: PWR_SW.L1, +5V_DC.VCC
